# Fritzing sketch robocar2 (saved by Fritzing 0.9.2b)
circuit board: 8.46667cm x 5.64444cm
breadboards: 1

parts:
  Part1 = Arduino Pro Mini v13
  Part2 = Motor Driver 1A Dual TB6612FNG
  S1 = Toggle Switch [package=THT]
  M1 = DC Motor
  M2 = DC Motor
  J1 = female pin header, 7 pins [form="♀ (female)"]

nets (from the breadboard view):
  N1: Part1.RAW, Part2.VM, S1.COM, S1.L2, J1.pin7
  GND: Part1.GND, Part2.GND, J1.pin6
  N2: Part1.RESET, J1.pin5
  VCC: Part1.VCC, Part2.VCC, J1.pin4
  N3: Part1.A3, J1.pin3
  N4: Part1.A2, J1.pin2
  N5: Part1.A1, J1.pin1
  N6: Part1.D9_PWM, Part2.PWMB
  N7: Part1.D8, Part2.BIN2
  N8: Part1.D7, Part2.BIN1
  N9: Part1.D6_PWM, Part2.STBY
  N10: Part1.D5_PWM, Part2.AIN1
  N11: Part1.D4, Part2.AIN2
  N12: Part1.D3_PWM, Part2.PWMA
  N13: Part2.B01, M2.pin_2
  N14: Part2.B02, M2.pin_1
  N15: Part2.A02, M1.pin_2
  N16: Part2.A01, M1.pin_1
